# Fritzing sketch rgb-led-strips (saved by Fritzing 0.9.5d)

parts:
  WeMos_D1_Mini1 = WeMos D1 Mini
  C1_100uF = Electrolytic Capacitor [capacitance=1μF package="0405 [SMD, electrolytic]"]
  RGB_SMD_LED1 = SMD RGB LED (WS2812B) [package=5050]
  Part1 = Logic Level Converter
  R1_100_Ohm = Resistor [package="2010 [SMD]"]
  GND_+5V = Camdenboss CTB0158-2 [part_number=CTB0158-2 package=THT]  # not connected

nets:
  N1: WeMos_D1_Mini1.3V3, Part1.LV
  5V: WeMos_D1_Mini1.5V, C1_100uF.+, RGB_SMD_LED1.VDD
  N2: WeMos_D1_Mini1.D4, Part1.TX_LV
  N3: WeMos_D1_Mini1.G, C1_100uF.-, RGB_SMD_LED1.VSS
  N4: RGB_SMD_LED1.DIN, R1_100_Ohm.Pin_1
  N5: Part1.RX_HV, R1_100_Ohm.Pin_0

notes:
  RGB-LED-STRIPS by luk6xff (2021)

custom parts:
  SMD RGB LED (WS2812B): The WS2812B is an RGB LED with a WS2811 control IC built right into the LED. Its improvement over its WS2812 ancestor is the reduction to 4 pins (a single power supply instead of 2) and dropping the requirement for the external resistors. The manufacturer says it has a better reverse connect protection.
  Resistor: Resistor Basic schematic elements and footprints for 0603, 1206, and PTH resistors.
